# Fritzing sketch BluefruitLE (saved by Fritzing 0.8.7b)
breadboards: 1

parts:
  Part1 = Arduino Uno (Rev3) - ICSP
  RF1 = nRF8001 Bluetooth LE Breakout
  neopixel1 = Neopixel Ring 16

nets:
  N1: Part1.ICSP_MOSI, Part1.D11_PWM/MOSI, RF1.MOSI
  GND: Part1.GND, RF1.GND, neopixel1.GND
  N2: Part1.D9_PWM, RF1.RST
  N3: Part1.D10_PWM/SS, RF1.REQ
  N4: Part1.D12/MISO, RF1.MISO
  N5: Part1.D13/SCK, RF1.SCK
  N6: Part1.D2, RF1.RDY
  N7: Part1.D5_PWM, neopixel1.IN
  5V: Part1.5V, RF1.VIN, neopixel1.VCC

custom parts:
  nRF8001 Bluetooth LE Breakout: nRF8001 Breakout Board
  Neopixel Ring 16: Neopixel Ring x16
